# Fritzing sketch GateOpener (saved by Fritzing 0.9.3b)
circuit board: 8.46667cm x 5.64444cm
breadboards: 1

parts:
  part = ESP8266 WiFi Module [part_number=ESP8266]
  U2 = V_REG_LD1117VXX [package=78xxl]
  2N2222 = NPN-Transistor [package="TO92 [THT]"]
  Hookup = Header 3 [package=molex-1x3_lock]
  C1 = Electrolytic Capacitor [capacitance=100nF package="100 mil [THT, electrolytic]"]
  C2 = Electrolytic Capacitor [capacitance=10µF package="100 mil [THT, electrolytic]"]
  part_2 = Resistor [tolerance=±5% resistance=1k package=THT]

nets:
  N1: part.VCC, part.RST, part.CH_PD, U2.OUT, C2.+
  N2: part.GPIO_2, part_2.Pin_0
  GND: part.GND, U2.GND, Hookup.2, C1.-, C2.-
  N3: U2.IN, 2N2222.C, Hookup.1, C1.+
  N4: 2N2222.E, Hookup.3
  N5: 2N2222.B, part_2.Pin_1

custom parts:
  ESP8266 WiFi Module: Generic WiFi Module based on the ESP8266 with onboard PCB antenna and UART communications
